# Fritzing sketch arduinoponia (saved by Fritzing 0.9.3b)
breadboards: 1

parts:
  U1 = 74HC595 [package="DIP16 [THT]"]  # not connected
  Componente1 = Arduino Uno (Rev3) - ICSP
  LED1 = smd LED [color="Yellow (595nm)" package="0805 [SMD]"]
  LED2 = smd LED [color="Yellow (595nm)" package="0805 [SMD]"]
  LED3 = smd LED [color="Yellow (595nm)" package="0805 [SMD]"]
  LED4 = smd LED [color="Green (570nm)" package="0805 [SMD]"]
  LED5 = smd LED [color="Green (570nm)" package="0805 [SMD]"]
  LED6 = smd LED [color="Green (570nm)" package="0805 [SMD]"]
  S1 = SWITCH-MOMENTARY-2 [package=tactile-pth-12mm]  # not connected
  R1 = Resistor [tolerance=±5% resistance=470 package=THT]
  R2 = Resistor [tolerance=±5% resistance=470 package=THT]
  R3 = Resistor [tolerance=±5% resistance=470 package=THT]
  R4 = Resistor [tolerance=±5% resistance=470 package=THT]
  R5 = Resistor [tolerance=±5% resistance=470 package=THT]
  R6 = Resistor [tolerance=±5% resistance=470 package=THT]
  R7 = Resistor [tolerance=±5% resistance=10k package="2512 [SMD]"]
  R8 = Resistor [tolerance=±5% resistance=10k package="2512 [SMD]"]
  R11 = Resistor [tolerance=±5% resistance=10k package="2512 [SMD]"]
  R12 = Resistor [tolerance=±5% resistance=10k package="2512 [SMD]"]
  KY-1 = Keyes Relay [package=THT]

nets:
  N1: Componente1.A0, R8.Pin_1
  N2: Componente1.A1, R11.Pin_1
  N3: Componente1.A2, R12.Pin_1
  N4: Componente1.GND, LED1.anode, LED2.anode, LED3.anode, LED4.anode, LED5.anode, LED6.anode, R7.Pin_1, R8.Pin_0, R11.Pin_0, R12.Pin_0, KY-1.ground
  N5: Componente1.D7, KY-1.signal
  N6: Componente1.5V, KY-1.power
  N7: LED1.cathode, R1.Pin_0
  N8: LED2.cathode, R2.Pin_0
  N9: LED3.cathode, R3.Pin_0
  N10: LED4.cathode, R4.Pin_0
  N11: LED5.cathode, R6.Pin_0
  N12: LED6.cathode, R5.Pin_0

notes:
  CLOCK
  LATCH
  DATA
  SENSORES
  ESTADO
  CAMBIAR SENSOR
  SENSOR #1
  DATA SENSOR #1
  SENSOR #2
  DATA SENSOR #2
  DATA SENSOR #3
  SENSOR #3
  RELAY SWITCH

custom parts:
  Keyes Relay: The Keyes 5V relay module is suitable for SCM development, home appliance control. It uses a 5V~12V TIL control signal which can control DC / AC signal.
