# Fritzing sketch hacklab_auto_controlRemoto (saved by Fritzing 0.9.3b)
breadboards: 1
perfboards: 1

parts:
  M1 = DC Motor
  M2 = DC Motor
  Componente2 = Adafruit Motor/Stepper/Servo Shield [part_number="Adafruit #1438"]
  R1 = Resistor [tolerance=±5% resistance=10k package="1206 [SMD]"]
  R2 = Resistor [tolerance=±5% resistance=10k package="1206 [SMD]"]
  R3 = Resistor [tolerance=±5% resistance=10k package="1206 [SMD]"]
  R4 = Resistor [tolerance=±5% resistance=10k package="1206 [SMD]"]
  J1 = shrouded pin header, 6 pins [form="♂ (shrouded male)"]
  S8 = Pushbutton [package="[SMD]"]
  S9 = Pushbutton [package="[SMD]"]
  S10 = Pushbutton [package="[SMD]"]
  S11 = Pushbutton [package="[SMD]"]

nets:
  N1: M1.pin_1, Componente2.M3B
  N2: M1.pin_2, Componente2.M3A
  N3: M2.pin_1, Componente2.M1B
  N4: M2.pin_2, Componente2.M1A
  N5: R1.Pin_0, J1.pin3, S8.Pin_1, S8.Pin_2
  N6: R2.Pin_0, J1.pin6, S11.Pin_1, S11.Pin_2
  N7: R2.Pin_1, J1.pin2
  N8: R3.Pin_1, S9.Pin_3, S9.Pin_4
  N9: R4.Pin_1, S10.Pin_3, S10.Pin_4
  N10: J1.pin1, J1.pin4, S9.Pin_1, S9.Pin_2
  N11: J1.pin5, S10.Pin_1, S10.Pin_2
  N12: S8.Pin_3, S8.Pin_4
  N13: S11.Pin_3, S11.Pin_4

notes:
  CONTROL REMOTO
  DATA CONTROL REMOTO

custom parts:
  Adafruit Motor/Stepper/Servo Shield: The original Adafruit Motorshield kit is one of our most beloved kits, which is why we decided to make something even better. We have upgraded the shield kit to make the bestest, easiest way to drive DC and Stepper motors. This shield will make quick work of your next robotics project! We kept the ability to drive up to 4 DC motors or 2 stepper motors, but added many improvements: Instead of a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
