# Fritzing sketch hacklab_auto_servo (saved by Fritzing 0.9.3b)

parts:
  M1 = DC Motor
  M2 = DC Motor
  Componente2 = Adafruit Motor/Stepper/Servo Shield [part_number="Adafruit #1438"]
  hc-sr1 = hc-sr04
  J1 = Basic Servo

nets:
  N1: M1.pin_1, Componente2.M3B
  N2: M1.pin_2, Componente2.M3A
  N3: M2.pin_1, Componente2.M1B
  N4: M2.pin_2, Componente2.M1A
  GND: Componente2.GND, hc-sr1.GND, J1.gnd
  VCC: Componente2.+5V, hc-sr1.VCC, J1.vcc
  N5: Componente2.D9, J1.pulse
  N6: Componente2.AD0, hc-sr1.Trig
  N7: Componente2.AD1, hc-sr1.Echo

custom parts:
  Adafruit Motor/Stepper/Servo Shield: The original Adafruit Motorshield kit is one of our most beloved kits, which is why we decided to make something even better. We have upgraded the shield kit to make the bestest, easiest way to drive DC and Stepper motors. This shield will make quick work of your next robotics project! We kept the ability to drive up to 4 DC motors or 2 stepper motors, but added many improvements: Instead of a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
